// Logisim project HW2-(刘恒澈)-(57854329).circ as structural Verilog: 12 circuits, main circuit Q1
module Q1 (
  input  in_1,
  output out_2,
  output out_3
);

  wire clock_1_out, nand_1_out, nand_2_out, nand_3_out, nand_4_out, nand_5_out, nand_6_out, not_1_out;

  Clock clock_1 (.out(clock_1_out));
  not not_1 (not_1_out, clock_1_out);
  nand nand_1 (nand_1_out, in_1, not_1_out);
  nand nand_2 (nand_2_out, nand_1_out, not_1_out);
  nand nand_3 (nand_3_out, nand_1_out, nand_4_out);
  nand nand_4 (nand_4_out, nand_3_out, nand_2_out);
  nand nand_5 (nand_5_out, nand_3_out, clock_1_out);
  nand nand_6 (nand_6_out, clock_1_out, nand_4_out);
  nand nand_7 (out_2, nand_5_out, out_3);
  nand nand_8 (out_3, out_2, nand_6_out);
endmodule

module Q2_2 (
  input  i1,
  input  i2,
  input  i3,
  output o1,
  output _02,
  output _03,
  output _04
);

  Q2_2_o1 _01 (.in_1(i1), .in_2(i2), .in_3(i3), .out_4(o1));
  Q2_2_o2 u__02 (.in_1(i1), .in_2(i2), .in_3(i3), .out_4(_02));
  Q2_2_o3 u__03 (.in_1(i1), .in_2(i2), .in_3(i3), .out_4(_03));
  Q2_2_o4 u__04 (.in_1(i1), .in_2(i2), .in_3(i3), .out_4(_04));
endmodule

module Q2_3 (
  input  in_1,
  input  in_2,
  input  in_3,
  input  in_4,
  input  in_5,
  input  in_6,
  input  in_7,
  input  in_8,
  input  in_9,
  output out_10,
  output out_11,
  output out_12,
  output out_13,
  output out_14
);

  wire full_adder_2_out_5, full_adder_3_out_5, full_adder_4_out_5;

  full_adder full_adder_1 (.in_1(in_1), .in_2(in_5), .in_3(full_adder_2_out_5), .out_4(out_11), .out_5(out_10));
  full_adder full_adder_2 (
    .in_1(in_2), .in_2(in_6), .in_3(full_adder_3_out_5), .out_4(out_12), .out_5(full_adder_2_out_5));
  full_adder full_adder_3 (
    .in_1(in_3), .in_2(in_7), .in_3(full_adder_4_out_5), .out_4(out_13), .out_5(full_adder_3_out_5));
  full_adder full_adder_4 (.in_1(in_4), .in_2(in_8), .in_3(in_9), .out_4(out_14), .out_5(full_adder_4_out_5));
endmodule

module Q2_4 (
  input  i1,
  input  i2,
  input  i3,
  output o1,
  output o2,
  output o3,
  output o4
);

  wire q2_2_1__02, q2_2_1__03, q2_2_1__04, q2_2_1_o1, x_2_1_out_4, x_2_1_out_5, x_2_1_out_6, x_2_1_out_7;

  Q2_2 q2_2_1 (.i1(i1), .i2(i2), .i3(i3), .o1(q2_2_1_o1), ._02(q2_2_1__02), ._03(q2_2_1__03), ._04(q2_2_1__04));
  x_2_2 x_2_1 (
    .in_1(i1), .in_2(i2), .in_3(i3), .out_4(x_2_1_out_4), .out_5(x_2_1_out_5), .out_6(x_2_1_out_6),
    .out_7(x_2_1_out_7));
  Q2_3 q2_3_1 (
    .in_1(q2_2_1_o1), .in_2(q2_2_1__02), .in_3(q2_2_1__03), .in_4(q2_2_1__04), .in_5(x_2_1_out_4),
    .in_6(x_2_1_out_5), .in_7(x_2_1_out_6), .in_8(x_2_1_out_7), .in_9(1'b0), .out_11(o1), .out_12(o2),
    .out_13(o3), .out_14(o4));  // open: out_10
endmodule

module Q2_2_o1 (
  input  in_1,
  input  in_2,
  input  in_3,
  output out_4
);

  wire and_1_out, and_2_out, not_1_out, not_2_out;

  not not_1 (not_1_out, in_1);
  not not_2 (not_2_out, in_3);
  and and_1 (and_1_out, in_3, in_2, in_1);
  and and_2 (and_2_out, not_1_out, in_2, not_2_out);
  or or_1 (out_4, and_1_out, and_2_out);
endmodule

module Q2_2_o2 (
  input  in_1,
  input  in_2,
  input  in_3,
  output out_4
);

  wire and_1_out, and_2_out, and_3_out, not_1_out, not_2_out, not_3_out;

  not not_1 (not_1_out, in_1);
  not not_2 (not_2_out, in_2);
  not not_3 (not_3_out, in_3);
  and and_1 (and_1_out, not_1_out, in_3);
  and and_2 (and_2_out, not_1_out, not_2_out, not_3_out);
  and and_3 (and_3_out, not_3_out, not_2_out, in_1);
  or or_1 (out_4, and_1_out, and_2_out, and_3_out);
endmodule

module Q2_2_o3 (
  input  in_1,
  input  in_2,
  input  in_3,
  output out_4
);

  wire and_1_out, and_2_out, and_3_out, not_1_out, not_2_out, not_3_out;

  and and_1 (and_1_out, in_3, in_1, not_2_out);
  not not_1 (not_1_out, in_1);
  not not_2 (not_2_out, in_2);
  not not_3 (not_3_out, in_3);
  and and_2 (and_2_out, not_1_out, not_2_out, in_3);
  and and_3 (and_3_out, in_1, in_2, not_3_out);
  or or_1 (out_4, and_1_out, and_2_out, and_3_out);
endmodule

module Q2_2_o4 (
  input  in_1,
  input  in_2,
  input  in_3,
  output out_4
);

  wire and_1_out, not_1_out, not_2_out, not_3_out;

  not not_1 (not_1_out, in_1);
  not not_2 (not_2_out, in_2);
  not not_3 (not_3_out, in_3);
  and and_1 (and_1_out, not_1_out, not_2_out, not_3_out);
  or or_1 (out_4, and_1_out, in_3);
endmodule

module full_adder (
  input  in_1,
  input  in_2,
  input  in_3,
  output out_4,
  output out_5
);

  wire and_1_out, and_2_out, and_3_out, xor_1_out;

  and and_1 (and_1_out, in_1, in_2);
  and and_2 (and_2_out, in_1, in_3);
  and and_3 (and_3_out, in_2, in_3);
  xor xor_1 (xor_1_out, in_1, in_2);
  xor xor_2 (out_4, xor_1_out, in_3);
  or or_1 (out_5, and_1_out, and_2_out, and_3_out);
endmodule

module x_2 (
  input  in_1,
  input  in_2,
  input  in_3,
  output out_4,
  output out_5,
  output out_6,
  output out_7
);


  assign out_4 = 1'b0;
  assign out_5 = 1'b0;
  assign out_6 = in_1;
  assign out_7 = in_2;
endmodule

module x_2_2 (
  input  in_1,
  input  in_2,
  input  in_3,
  output out_4,
  output out_5,
  output out_6,
  output out_7
);

  wire not_1_out, not_2_out, not_3_out, not_4_out, x_2_1_out_4, x_2_1_out_5, x_2_1_out_6, x_2_1_out_7;

  x_2 x_2_1 (
    .in_1(in_1), .in_2(in_2), .in_3(in_3), .out_4(x_2_1_out_4), .out_5(x_2_1_out_5), .out_6(x_2_1_out_6),
    .out_7(x_2_1_out_7));
  not not_1 (not_1_out, x_2_1_out_4);
  not not_2 (not_2_out, x_2_1_out_5);
  not not_3 (not_3_out, x_2_1_out_6);
  not not_4 (not_4_out, x_2_1_out_7);
  Q2_3 q2_3_1 (
    .in_1(not_1_out), .in_2(not_2_out), .in_3(not_3_out), .in_4(not_4_out), .in_5(1'b0), .in_6(1'b0),
    .in_7(1'b0), .in_8(1'b1), .in_9(1'b0), .out_11(out_4), .out_12(out_5), .out_13(out_6), .out_14(out_7));  // open: out_10
endmodule

module test (
  input  x1,
  input  x2,
  input  x3,
  output o
);

  wire and_1_out, and_2_out, not_1_out, not_2_out, not_3_out;

  not not_1 (not_1_out, x1);
  not not_2 (not_2_out, x2);
  and and_1 (and_1_out, not_2_out, not_3_out);
  not not_3 (not_3_out, x3);
  and and_2 (and_2_out, not_1_out, x3);
  or or_1 (o, and_2_out, and_1_out);
endmodule
