// Logisim project HW3 add pipeline-1.circ as structural Verilog: 17 circuits, main circuit main
module main (
);

  wire ALU_bltsignal, and_1_out, branch___jump, clock, clock_1_out, Control_regdst, EX___MEM_halt_2, exwrite,
       halt, hazard_1_flushid, hazard_1_flushif, hazard_1_stallid, hazard_1_stallif, memwrite,
       regread_1_r1read, regread_1_r2read, reset, rread, rwrite, W;
  wire [1:0] Control_memtoreg, EX___MEM_m_2, EX___MEM_wb_2, ID___EX_wb_2, MEM___WB_wb_2;
  wire [2:0] ALU_control_out_3, Control_aluop, ex, ID___EX_m_2, mem, multiplexer_4_out, w_t;
  wire [2:2] Control_regwrite;
  wire [3:0] IF___ID_instru_2_2;
  wire [3:2] ID___EX_m_2_2;
  wire [4:0] Control_memread;
  wire [6:0] Control_alusrc, ID___EX_ex_2;
  wire [11:0] IF___ID_instru_2;
  wire [15:0] adder_1_out, adder_2_out, ALU_max, ALU_min, ALU_out_7, bit_extender_1_out, EX___MEM_a_2,
       EX___MEM_d_2, EX___MEM_max_2, EX___MEM_min_2, ID___EX_imm_2, ID___EX_pc_1_2, ID___EX_r1_2,
       ID___EX_r2_2, IF___ID_pc_1_2, MEM___WB_a_2, MEM___WB_d_2, MEM___WB_max_2, MEM___WB_min_2,
       MinusControl_out_2, multiplexer_1_out, multiplexer_2_out, multiplexer_5_out, multiplexer_6_out,
       multiplexer_7_out, multiplexer_8_out, PC_q, Ra_Register_data1, ram_1_data, RegisterFile_data1,
       RegisterFile_data2, rom_1_data, subtractor_1_out;

  Multiplexer #(.width(16), .enable("false")) multiplexer_1 (
    .in0(adder_1_out), .in1(adder_2_out), .out(multiplexer_1_out), .sel(branch___jump));
  Clock clock_1 (.out(clock_1_out));
  Multiplexer #(.width(16), .enable("false")) multiplexer_2 (
    .in0(multiplexer_1_out), .in1(multiplexer_5_out), .out(multiplexer_2_out), .sel(rread));
  Multiplexer #(.enable("false")) multiplexer_3 (.in0(clock_1_out), .in1(1'b0), .out(clock), .sel(halt));
  Button button_1 (.out(reset));
  minus_64 MinusControl (.in_1(multiplexer_2_out), .out_2(MinusControl_out_2));
  Register #(.width(16)) PC (.D(MinusControl_out_2), .en(hazard_1_stallif), .Q(PC_q), .clk(clock), .clr(reset));
  Adder #(.width(16)) adder_1 (.a(PC_q), .b(16'h1), .out(adder_1_out));  // open: cin, cout
  regread regread_1 (
    .o1(IF___ID_instru_2_2[3]), .o2(IF___ID_instru_2_2[2]), .o3(IF___ID_instru_2_2[1]),
    .r1read(regread_1_r1read), .o4(IF___ID_instru_2_2[0]), .f1(IF___ID_instru_2[0]),
    .f2(IF___ID_instru_2[1]), .f3(IF___ID_instru_2[2]), .r2read(regread_1_r2read));
  IF_ID IF___ID (
    .PC_1(adder_1_out), .instru(rom_1_data), .PC_1_2(IF___ID_pc_1_2),
    .instru_2({IF___ID_instru_2_2, IF___ID_instru_2}), .clock(clock), .reset(hazard_1_flushif),
    .enable(hazard_1_stallid));
  ROM #(.addrWidth(16), .dataWidth(16)) rom_1 (.addr(PC_q), .data(rom_1_data));  // open: sel
  hazard hazard_1 (
    .r1read(regread_1_r1read), .r2(IF___ID_instru_2[8:6]), .r1(IF___ID_instru_2[11:9]),
    .branch___jump(branch___jump), .flushID(hazard_1_flushid), .r2read(regread_1_r2read),
    .stallIF(hazard_1_stallif), .stallID(hazard_1_stallid), .flushIF(hazard_1_flushif), .in_1(clock),
    .w(w_t), .ex(ex), .mem(mem), .memwrite(memwrite), .exwrite(exwrite), .W_2(W));
  assign bit_extender_1_out = {{10{1'b0}}, IF___ID_instru_2[5:0]};  // Bit_Extender bit_extender_1
  ra_register Ra_Register (
    .Write(rwrite), .in_2(adder_1_out), .clock(clock), .reset(reset), .Read(rread), .Data1(Ra_Register_data1));
  control Control (
    .opcode(IF___ID_instru_2_2), .RegDst(Control_regdst), .ALUSrc(Control_alusrc[0]),
    .MemtoReg(Control_memtoreg), .RegWrite(Control_regwrite[2]), .MemRead(Control_memread[0]),
    .MemWrite(Control_memread[1]), .Branch(Control_memread[2]), .Jump(Control_memread[3]),
    .ALUOp(Control_aluop), .RaRead(Control_memread[4]), .RaWrite(Control_alusrc[4]),
    .halt(Control_alusrc[5]), .li(Control_alusrc[6]));
  Multiplexer #(.width(3), .enable("false")) multiplexer_4 (
    .in0(IF___ID_instru_2[8:6]), .in1(IF___ID_instru_2[5:3]), .out(multiplexer_4_out), .sel(Control_regdst));
  Multiplexer #(.width(16), .enable("false")) multiplexer_5 (
    .in0({16{1'b0}}), .in1(Ra_Register_data1), .out(multiplexer_5_out), .sel(rread));
  register RegisterFile (
    .Write(W), .Write_Register(w_t), .Register_Data(multiplexer_8_out), .clock(clock),
    .Data1(RegisterFile_data1), .Data2(RegisterFile_data2), .reset(reset),
    .Read_Regisiter2(IF___ID_instru_2[8:6]), .Read_Regisiter1(IF___ID_instru_2[11:9]));
  ID_EX ID___EX (
    .WB({Control_regwrite[2], Control_memtoreg}), .M(Control_memread),
    .EX({Control_alusrc[6:4], Control_aluop, Control_alusrc[0]}), .PC_1(IF___ID_pc_1_2),
    .r1(RegisterFile_data1), .r2(RegisterFile_data2), .imm(bit_extender_1_out),
    .WB_2({exwrite, ID___EX_wb_2}), .M_2({ID___EX_m_2[2], ID___EX_m_2_2, ID___EX_m_2[1:0]}),
    .EX_2({ID___EX_ex_2[6:5], rwrite, ID___EX_ex_2[3:0]}), .PC_1_2(ID___EX_pc_1_2), .r1_2(ID___EX_r1_2),
    .r2_2(ID___EX_r2_2), .imm_2(ID___EX_imm_2), .clock(clock), .reset(hazard_1_flushid),
    .w(multiplexer_4_out), .w_2(ex));
  and and_1 (and_1_out, ID___EX_m_2_2[2], ALU_bltsignal);
  or or_1 (branch___jump, and_1_out, ID___EX_m_2_2[3]);
  Multiplexer #(.width(16), .enable("false")) multiplexer_6 (
    .in0(ID___EX_r2_2), .in1(ID___EX_imm_2), .out(multiplexer_6_out), .sel(ID___EX_ex_2[0]));
  alu_control ALU_control (.Funct(ID___EX_imm_2[2:0]), .ALUOp(ID___EX_ex_2[3:1]), .out_3(ALU_control_out_3));
  Multiplexer #(.width(16), .enable("false")) multiplexer_7 (
    .in0(ID___EX_r1_2), .in1({16{1'b0}}), .out(multiplexer_7_out), .sel(ID___EX_ex_2[6]));
  Subtractor #(.width(16)) subtractor_1 (.a(ID___EX_imm_2), .b(16'h1), .out(subtractor_1_out));  // open: bin, bout
  ALU ALU (
    .d1(multiplexer_7_out), .d2(multiplexer_6_out), .bltsignal(ALU_bltsignal), .out_7(ALU_out_7),
    .alusignal(ALU_control_out_3), .max(ALU_max), .min(ALU_min));
  EX_MEM EX___MEM (
    .WB({exwrite, ID___EX_wb_2}), .M(ID___EX_m_2), .max(ALU_max), .min(ALU_min), .A(ALU_out_7),
    .D(ID___EX_r2_2), .WB_2({memwrite, EX___MEM_wb_2}), .M_2({rread, EX___MEM_m_2}), .max_2(EX___MEM_max_2),
    .min_2(EX___MEM_min_2), .A_2(EX___MEM_a_2), .D_2(EX___MEM_d_2), .clock(clock), .reset(reset), .w(ex),
    .w_2(mem), .halt(ID___EX_ex_2[5]), .halt_2(EX___MEM_halt_2));
  Adder #(.width(16)) adder_2 (.a(ID___EX_pc_1_2), .b(subtractor_1_out), .out(adder_2_out));  // open: cin, cout
  RAM #(.addrWidth(16), .dataWidth(16), .bus("separate")) ram_1 (
    .addr(EX___MEM_a_2), .din(EX___MEM_d_2), .data(ram_1_data), .str(EX___MEM_m_2[1]), .clk(clock),
    .ld(EX___MEM_m_2[0]), .clr(reset));  // open: sel
  MEM_WB MEM___WB (
    .WB({memwrite, EX___MEM_wb_2}), .max(EX___MEM_max_2), .min(EX___MEM_min_2), .D(ram_1_data),
    .A(EX___MEM_a_2), .WB_2({W, MEM___WB_wb_2}), .max_2(MEM___WB_max_2), .min_2(MEM___WB_min_2),
    .D_2(MEM___WB_d_2), .A_2(MEM___WB_a_2), .clock(clock), .reset(reset), .w(mem), .w_2(w_t),
    .halt(EX___MEM_halt_2), .halt_2(halt));
  Multiplexer #(.select(2), .width(16), .enable("false")) multiplexer_8 (
    .in0(MEM___WB_a_2), .in1(MEM___WB_d_2), .in2(MEM___WB_max_2), .in3(MEM___WB_min_2),
    .out(multiplexer_8_out), .sel(MEM___WB_wb_2));

  // Notes on the sheet:
  //   contents of rom_1 (hex, n*v repeats v):
  //   d001 d04a d082 7 48 c47f e000
endmodule

module ALU (
  input  [15:0] d1,
  input  [15:0] d2,
  input  [2:0] alusignal,
  output [15:0] max,
  output [15:0] min,
  output bltsignal,
  output [15:0] out_7
);

  wire comparator_1_gt;
  wire [15:0] adder_1_out, and_1_out, multiplier_1_out, negator_1_out, or_1_out, shifter_1_out,
       shifter_2_out, shifter_3_out;

  Multiplexer #(.width(16), .enable("false")) multiplexer_1 (.in0(d1), .in1(d2), .out(max), .sel(bltsignal));
  Multiplexer #(.width(16), .enable("false")) multiplexer_2 (.in0(d1), .in1(d2), .out(min), .sel(comparator_1_gt));
  Comparator #(.width(16), .mode("unsigned")) comparator_1 (
    .a(d1), .b(d2), .gt(comparator_1_gt), .lt(bltsignal));  // open: eq
  Adder #(.width(16)) adder_1 (.a(d1), .b(d2), .out(adder_1_out));  // open: cin, cout
  assign and_1_out = d1 & d2;  // AND_Gate and_1, 16 bits wide
  assign or_1_out = d1 | d2;  // OR_Gate or_1, 16 bits wide
  Multiplier #(.width(16)) multiplier_1 (.a(d1), .b(d2), .out(multiplier_1_out));  // open: cin, cout
  Shifter #(.width(16)) shifter_1 (.in(d1), .\dist (d2[3:0]), .out(shifter_1_out));
  Shifter #(.width(16), .shift("lr")) shifter_2 (.in(d1), .\dist (d2[3:0]), .out(shifter_2_out));
  Shifter #(.width(16), .shift("ar")) shifter_3 (.in(d1), .\dist (d2[3:0]), .out(shifter_3_out));
  Negator #(.width(16)) negator_1 (.in(d1), .out(negator_1_out));
  Multiplexer #(.select(3), .width(16)) multiplexer_3 (
    .in0(adder_1_out), .in1(and_1_out), .in2(or_1_out), .in3(multiplier_1_out), .in4(shifter_1_out),
    .in5(shifter_2_out), .in6(shifter_3_out), .in7(negator_1_out), .out(out_7), .sel(alusignal), .en(1'b1));
endmodule

module alu_control (
  input  [2:0] Funct,
  input  [2:0] ALUOp,
  output [2:0] out_3
);

  wire comparator_1_eq;
  wire [2:0] subtractor_1_out;

  Subtractor #(.width(3)) subtractor_1 (.a(ALUOp), .b(3'b001), .out(subtractor_1_out));  // open: bin, bout
  Comparator #(.width(3)) comparator_1 (.a(ALUOp), .b(3'b000), .eq(comparator_1_eq));  // open: gt, lt
  Multiplexer #(.width(3), .enable("false")) multiplexer_1 (
    .in0(subtractor_1_out), .in1(Funct), .out(out_3), .sel(comparator_1_eq));
endmodule

module register (
  input  Write,
  input  [2:0] Write_Register,
  input  [15:0] Register_Data,
  input  [2:0] Read_Regisiter2,
  input  [2:0] Read_Regisiter1,
  input  clock,
  input  reset,
  output [15:0] Data1,
  output [15:0] Data2
);

  wire and_1_out, and_2_out, and_3_out, and_4_out, and_5_out, and_6_out, and_7_out, and_8_out,
       decoder_1_out0, decoder_1_out1, decoder_1_out2, decoder_1_out3, decoder_1_out4, decoder_1_out5,
       decoder_1_out6, decoder_1_out7;
  wire [15:0] register_1_q, register_2_q, register_3_q, register_4_q, register_5_q, register_6_q,
       register_7_q, register_8_q;

  Decoder #(.select(3), .enable("false")) decoder_1 (
    .out0(decoder_1_out0), .out1(decoder_1_out1), .out2(decoder_1_out2), .out3(decoder_1_out3),
    .out4(decoder_1_out4), .out5(decoder_1_out5), .out6(decoder_1_out6), .out7(decoder_1_out7),
    .sel(Write_Register));
  and and_1 (and_1_out, Write, decoder_1_out0);
  and and_2 (and_2_out, Write, decoder_1_out1);
  and and_3 (and_3_out, Write, decoder_1_out2);
  and and_4 (and_4_out, Write, decoder_1_out3);
  and and_5 (and_5_out, Write, decoder_1_out4);
  and and_6 (and_6_out, Write, decoder_1_out5);
  and and_7 (and_7_out, Write, decoder_1_out6);
  and and_8 (and_8_out, Write, decoder_1_out7);
  Register #(.width(16)) register_1 (.D(Register_Data), .en(and_1_out), .Q(register_1_q), .clk(clock), .clr(reset));
  Register #(.width(16)) register_2 (.D(Register_Data), .en(and_2_out), .Q(register_2_q), .clk(clock), .clr(reset));
  Register #(.width(16)) register_3 (.D(Register_Data), .en(and_3_out), .Q(register_3_q), .clk(clock), .clr(reset));
  Register #(.width(16)) register_4 (.D(Register_Data), .en(and_4_out), .Q(register_4_q), .clk(clock), .clr(reset));
  Register #(.width(16)) register_5 (.D(Register_Data), .en(and_5_out), .Q(register_5_q), .clk(clock), .clr(reset));
  Register #(.width(16)) register_6 (.D(Register_Data), .en(and_6_out), .Q(register_6_q), .clk(clock), .clr(reset));
  Register #(.width(16)) register_7 (.D(Register_Data), .en(and_7_out), .Q(register_7_q), .clk(clock), .clr(reset));
  Register #(.width(16)) register_8 (.D(Register_Data), .en(and_8_out), .Q(register_8_q), .clk(clock), .clr(reset));
  Multiplexer #(.select(3), .width(16), .enable("false")) multiplexer_1 (
    .in0(register_1_q), .in1(register_2_q), .in2(register_3_q), .in3(register_4_q), .in4(register_5_q),
    .in5(register_6_q), .in6(register_7_q), .in7(register_8_q), .out(Data1), .sel(Read_Regisiter1));
  Multiplexer #(.select(3), .width(16), .enable("false")) multiplexer_2 (
    .in0(register_1_q), .in1(register_2_q), .in2(register_3_q), .in3(register_4_q), .in4(register_5_q),
    .in5(register_6_q), .in6(register_7_q), .in7(register_8_q), .out(Data2), .sel(Read_Regisiter2));
endmodule

module ra_control (
  input  a,
  input  b,
  input  c,
  input  d,
  output RaRead,
  output RaWrite
);

  wire not_1_out, not_2_out;

  not not_1 (not_1_out, a);
  not not_2 (not_2_out, b);
  and and_1 (RaRead, not_1_out, b, c, d);
  and and_2 (RaWrite, a, not_2_out, c, d);
endmodule

module control12 (
  input  a,
  input  b,
  input  c,
  input  d,
  output RegDst,
  output ALUSrc,
  output MemtoReg1,
  output MemtoReg0,
  output RegWrite,
  output MemRead,
  output MemWrite,
  output Branch,
  output Jump,
  output ALUOp2,
  output ALUOp1,
  output ALUOp0
);

  wire and_1_out, and_2_out, and_3_out, and_4_out, and_5_out, and_6_out, and_7_out, and_8_out, and_9_out,
       and_11_out, and_12_out, and_13_out, and_14_out, and_15_out, and_16_out, and_17_out, and_21_out,
       and_22_out, and_24_out, and_25_out, and_26_out, and_27_out, not_1_out, not_2_out, not_3_out,
       not_4_out, not_5_out, not_6_out, not_7_out, not_8_out, not_9_out, not_10_out, not_11_out, not_12_out,
       not_13_out, not_14_out, not_15_out, not_16_out, not_17_out, not_18_out, not_19_out, not_20_out,
       not_21_out, not_22_out, not_23_out, not_24_out, not_25_out, not_26_out, not_27_out, not_28_out,
       not_29_out, not_30_out, not_31_out, not_32_out, not_33_out, not_34_out, not_35_out, not_36_out,
       not_37_out, not_38_out, not_39_out, not_40_out, not_41_out, not_42_out, not_43_out, not_44_out,
       not_45_out, not_46_out, not_47_out, not_48_out, not_49_out, not_50_out, not_51_out, not_52_out,
       not_53_out;

  not not_1 (not_1_out, a);
  not not_2 (not_2_out, b);
  not not_3 (not_3_out, c);
  not not_4 (not_4_out, d);
  not not_5 (not_5_out, a);
  not not_6 (not_6_out, c);
  not not_7 (not_7_out, a);
  not not_8 (not_8_out, d);
  not not_9 (not_9_out, a);
  and and_1 (and_1_out, not_9_out, not_10_out, d);
  not not_10 (not_10_out, b);
  not not_11 (not_11_out, a);
  and and_2 (and_2_out, not_11_out, not_12_out, c);
  not not_12 (not_12_out, b);
  not not_13 (not_13_out, b);
  and and_3 (and_3_out, a, not_13_out, not_14_out);
  not not_14 (not_14_out, c);
  and and_4 (and_4_out, a, b, d);
  not not_15 (not_15_out, a);
  not not_16 (not_16_out, c);
  not not_17 (not_17_out, a);
  not not_18 (not_18_out, d);
  not not_19 (not_19_out, a);
  not not_20 (not_20_out, d);
  not not_21 (not_21_out, b);
  not not_22 (not_22_out, c);
  not not_23 (not_23_out, d);
  not not_24 (not_24_out, a);
  and and_5 (and_5_out, not_24_out, not_25_out);
  not not_25 (not_25_out, b);
  not not_26 (not_26_out, a);
  and and_6 (and_6_out, not_26_out, not_27_out);
  not not_27 (not_27_out, c);
  not not_28 (not_28_out, a);
  and and_7 (and_7_out, not_28_out, not_29_out);
  not not_29 (not_29_out, d);
  not not_30 (not_30_out, b);
  and and_8 (and_8_out, not_30_out, not_31_out, not_32_out);
  not not_31 (not_31_out, c);
  not not_32 (not_32_out, d);
  and and_9 (and_9_out, a, b, d);
  not not_33 (not_33_out, b);
  not not_34 (not_34_out, c);
  not not_35 (not_35_out, d);
  not not_36 (not_36_out, b);
  not not_37 (not_37_out, c);
  not not_38 (not_38_out, c);
  not not_39 (not_39_out, d);
  not not_40 (not_40_out, a);
  not not_41 (not_41_out, b);
  not not_42 (not_42_out, a);
  not not_43 (not_43_out, c);
  not not_44 (not_44_out, d);
  not not_45 (not_45_out, a);
  and and_10 (ALUOp1, not_45_out, not_46_out, c);
  not not_46 (not_46_out, b);
  not not_47 (not_47_out, a);
  not not_48 (not_48_out, b);
  not not_49 (not_49_out, a);
  not not_50 (not_50_out, c);
  not not_51 (not_51_out, d);
  not not_52 (not_52_out, b);
  not not_53 (not_53_out, c);
  and and_11 (and_11_out, not_1_out, not_2_out, not_3_out, not_4_out);
  or or_1 (RegDst, and_11_out, and_12_out, and_13_out);
  and and_12 (and_12_out, not_5_out, b, not_6_out, d);
  and and_13 (and_13_out, not_7_out, b, c, not_8_out);
  or or_2 (ALUSrc, and_1_out, and_2_out, and_3_out, and_4_out);
  and and_14 (and_14_out, not_15_out, b, not_16_out, d);
  or or_3 (MemtoReg1, and_14_out, and_15_out);
  and and_15 (and_15_out, not_17_out, b, c, not_18_out);
  and and_16 (and_16_out, not_19_out, b, c, not_20_out);
  or or_4 (MemtoReg0, and_16_out, and_17_out);
  and and_17 (and_17_out, a, not_21_out, not_22_out, not_23_out);
  or or_5 (RegWrite, and_5_out, and_6_out, and_7_out, and_8_out, and_9_out);
  and and_18 (MemRead, a, not_33_out, not_34_out, not_35_out);
  and and_19 (MemWrite, a, not_36_out, not_37_out, d);
  and and_20 (Branch, a, b, not_38_out, not_39_out);
  and and_21 (and_21_out, not_40_out, b, c, d);
  or or_6 (Jump, and_21_out, and_22_out);
  and and_22 (and_22_out, a, not_41_out, c);
  and and_23 (ALUOp2, not_42_out, b, not_43_out, not_44_out);
  and and_24 (and_24_out, not_47_out, not_48_out, d);
  and and_25 (and_25_out, not_49_out, b, not_50_out, not_51_out);
  and and_26 (and_26_out, a, not_52_out, not_53_out);
  and and_27 (and_27_out, a, b, d);
  or or_7 (ALUOp0, and_24_out, and_25_out, and_26_out, and_27_out);
endmodule

module control (
  input  [3:0] opcode,
  output RegDst,
  output ALUSrc,
  output [1:0] MemtoReg,
  output RegWrite,
  output MemRead,
  output MemWrite,
  output Branch,
  output Jump,
  output [2:0] ALUOp,
  output RaRead,
  output RaWrite,
  output halt,
  output li
);

  control12 control12_1 (
    .a(opcode[3]), .b(opcode[2]), .c(opcode[1]), .d(opcode[0]), .RegDst(RegDst), .ALUSrc(ALUSrc),
    .MemtoReg1(MemtoReg[1]), .MemtoReg0(MemtoReg[0]), .RegWrite(RegWrite), .MemRead(MemRead),
    .MemWrite(MemWrite), .Branch(Branch), .Jump(Jump), .ALUOp2(ALUOp[2]), .ALUOp1(ALUOp[1]), .ALUOp0(ALUOp[0]));
  ra_control ra_control_1 (
    .a(opcode[3]), .b(opcode[2]), .c(opcode[1]), .d(opcode[0]), .RaRead(RaRead), .RaWrite(RaWrite));
  Comparator #(.width(4)) comparator_1 (.a(opcode), .b(4'b1110), .eq(halt));  // open: gt, lt
  Comparator #(.width(4)) comparator_2 (.a(opcode), .b(4'b1101), .eq(li));  // open: gt, lt
endmodule

module ra_register (
  input  Write,
  input  [15:0] in_2,
  input  Read,
  input  clock,
  input  reset,
  output [15:0] Data1
);

  wire [15:0] register_1_q;

  Register #(.width(16)) register_1 (.D(in_2), .en(Write), .Q(register_1_q), .clk(clock), .clr(reset));
  assign Data1 = Read ? register_1_q : 16'bz;  // Controlled_Buffer controlled_buffer_1
endmodule

module PC (
  input  Clock,
  input  Reset,
  output [15:0] Address
);

  wire [15:0] adder_1_out;

  Register #(.width(16)) register_1 (.D(adder_1_out), .Q(Address), .clk(Clock), .clr(Reset));  // open: en
  Adder #(.width(16)) adder_1 (.a(Address), .b(16'h1), .out(adder_1_out));  // open: cin, cout
endmodule

module Memory_Control (
  input  w,
  input  r,
  output sel,
  output ld
);

  or or_1 (sel, w, r);

  assign ld = r;
endmodule

module minus_64 (
  input  [15:0] in_1,
  output [15:0] out_2
);

  wire comparator_1_gt;
  wire [15:0] subtractor_1_out;

  Subtractor #(.width(16)) subtractor_1 (.a(in_1), .b(16'h40), .out(subtractor_1_out));  // open: bin, bout
  Comparator #(.width(16), .mode("unsigned")) comparator_1 (
    .a(in_1), .b(16'h40), .gt(comparator_1_gt));  // open: eq, lt
  Multiplexer #(.width(16), .enable("false")) multiplexer_1 (
    .in0(in_1), .in1(subtractor_1_out), .out(out_2), .sel(comparator_1_gt));
endmodule

module IF_ID (
  input  [15:0] PC_1,
  input  [15:0] instru,
  input  clock,
  input  reset,
  input  enable,
  output [15:0] PC_1_2,
  output [15:0] instru_2
);

  Register #(.width(16)) register_1 (.D(PC_1), .en(enable), .Q(PC_1_2), .clk(clock), .clr(reset));
  Register #(.width(16)) register_2 (.D(instru), .en(enable), .Q(instru_2), .clk(clock), .clr(reset));
endmodule

module ID_EX (
  input  [2:0] WB,
  input  [4:0] M,
  input  [6:0] EX,
  input  [15:0] PC_1,
  input  [15:0] r1,
  input  [15:0] r2,
  input  [2:0] w,
  input  [15:0] imm,
  input  clock,
  input  reset,
  output [2:0] WB_2,
  output [4:0] M_2,
  output [6:0] EX_2,
  output [15:0] PC_1_2,
  output [15:0] r1_2,
  output [15:0] r2_2,
  output [2:0] w_2,
  output [15:0] imm_2
);

  Register #(.width(3)) register_1 (.D(WB), .en(1'b1), .Q(WB_2), .clk(clock), .clr(reset));
  Register #(.width(5)) register_2 (.D(M), .en(1'b1), .Q(M_2), .clk(clock), .clr(reset));
  Register #(.width(7)) register_3 (.D(EX), .en(1'b1), .Q(EX_2), .clk(clock), .clr(reset));
  Register #(.width(16)) register_4 (.D(PC_1), .en(1'b1), .Q(PC_1_2), .clk(clock), .clr(reset));
  Register #(.width(16)) register_5 (.D(r1), .en(1'b1), .Q(r1_2), .clk(clock), .clr(reset));
  Register #(.width(16)) register_6 (.D(r2), .en(1'b1), .Q(r2_2), .clk(clock), .clr(reset));
  Register #(.width(3)) register_7 (.D(w), .en(1'b1), .Q(w_2), .clk(clock), .clr(reset));
  Register #(.width(16)) register_8 (.D(imm), .en(1'b1), .Q(imm_2), .clk(clock), .clr(reset));
endmodule

module EX_MEM (
  input  [2:0] WB,
  input  [2:0] M,
  input  halt,
  input  [15:0] max,
  input  [15:0] min,
  input  [15:0] A,
  input  [15:0] D,
  input  [2:0] w,
  input  clock,
  input  reset,
  output [2:0] WB_2,
  output [2:0] M_2,
  output halt_2,
  output [15:0] max_2,
  output [15:0] min_2,
  output [15:0] A_2,
  output [15:0] D_2,
  output [2:0] w_2
);

  Register #(.width(3)) register_1 (.D(WB), .en(1'b1), .Q(WB_2), .clk(clock), .clr(reset));
  Register #(.width(3)) register_2 (.D(M), .en(1'b1), .Q(M_2), .clk(clock), .clr(reset));
  Register #(.width(1)) register_3 (.D(halt), .en(1'b1), .Q(halt_2), .clk(clock), .clr(reset));
  Register #(.width(16)) register_4 (.D(max), .en(1'b1), .Q(max_2), .clk(clock), .clr(reset));
  Register #(.width(16)) register_5 (.D(min), .en(1'b1), .Q(min_2), .clk(clock), .clr(reset));
  Register #(.width(16)) register_6 (.D(A), .en(1'b1), .Q(A_2), .clk(clock), .clr(reset));
  Register #(.width(16)) register_7 (.D(D), .en(1'b1), .Q(D_2), .clk(clock), .clr(reset));
  Register #(.width(3)) register_8 (.D(w), .en(1'b1), .Q(w_2), .clk(clock), .clr(reset));
endmodule

module MEM_WB (
  input  [2:0] WB,
  input  halt,
  input  [15:0] max,
  input  [15:0] min,
  input  [15:0] D,
  input  [2:0] w,
  input  [15:0] A,
  input  clock,
  input  reset,
  output [2:0] WB_2,
  output halt_2,
  output [15:0] max_2,
  output [15:0] min_2,
  output [15:0] D_2,
  output [2:0] w_2,
  output [15:0] A_2
);

  Register #(.width(3)) register_1 (.D(WB), .en(1'b1), .Q(WB_2), .clk(clock), .clr(reset));
  Register #(.width(1)) register_2 (.D(halt), .en(1'b1), .Q(halt_2), .clk(clock), .clr(reset));
  Register #(.width(16)) register_3 (.D(max), .en(1'b1), .Q(max_2), .clk(clock), .clr(reset));
  Register #(.width(16)) register_4 (.D(min), .en(1'b1), .Q(min_2), .clk(clock), .clr(reset));
  Register #(.width(16)) register_5 (.D(D), .en(1'b1), .Q(D_2), .clk(clock), .clr(reset));
  Register #(.width(3)) register_6 (.D(w), .en(1'b1), .Q(w_2), .clk(clock), .clr(reset));
  Register #(.width(16)) register_7 (.D(A), .en(1'b1), .Q(A_2), .clk(clock), .clr(reset));
endmodule

// HAZARD
module hazard (
  input  in_1,
  input  r1read,
  input  r2read,
  input  [2:0] ex,
  input  exwrite,
  input  [2:0] r2,
  input  [2:0] r1,
  input  [2:0] mem,
  input  memwrite,
  input  branch___jump,
  input  [2:0] w,
  input  W_2,
  output flushID,
  output stallIF,
  output stallID,
  output flushIF
);

  wire and_1_out, and_2_out, and_3_out, and_4_out, and_5_out, and_6_out, and_7_out, and_8_out, and_9_out,
       comparator_1_eq, comparator_2_eq, comparator_3_eq, comparator_4_eq, comparator_5_eq, comparator_6_eq,
       d_ff_1_q, d_ff_2_q, or_1_out, or_2_out, or_3_out, or_4_out;

  Comparator #(.width(3)) comparator_1 (.a(ex), .b(r2), .eq(comparator_1_eq));  // open: gt, lt
  Comparator #(.width(3)) comparator_2 (.a(ex), .b(r1), .eq(comparator_2_eq));  // open: gt, lt
  Comparator #(.width(3)) comparator_3 (.a(mem), .b(r2), .eq(comparator_3_eq));  // open: gt, lt
  Comparator #(.width(3)) comparator_4 (.a(mem), .b(r1), .eq(comparator_4_eq));  // open: gt, lt
  Comparator #(.width(3)) comparator_5 (.a(w), .b(r2), .eq(comparator_5_eq));  // open: gt, lt
  Comparator #(.width(3)) comparator_6 (.a(w), .b(r1), .eq(comparator_6_eq));  // open: gt, lt
  and and_1 (and_1_out, comparator_1_eq, r2read);
  and and_2 (and_2_out, comparator_2_eq, r1read);
  and and_3 (and_3_out, comparator_3_eq, r2read);
  and and_4 (and_4_out, comparator_4_eq, r1read);
  and and_5 (and_5_out, comparator_5_eq, r2read);
  and and_6 (and_6_out, comparator_6_eq, r1read);
  or or_1 (or_1_out, and_1_out, and_2_out);
  or or_2 (or_2_out, and_3_out, and_4_out);
  or or_3 (or_3_out, and_5_out, and_6_out);
  and and_7 (and_7_out, exwrite, or_1_out);
  or or_4 (or_4_out, and_7_out, and_8_out, and_9_out);
  and and_8 (and_8_out, memwrite, or_2_out);
  and and_9 (and_9_out, W_2, or_3_out);
  D_Flip_Flop #(.trigger("falling")) d_ff_1 (.clk(in_1), .D(or_4_out), .Q(d_ff_1_q));  // open: Qn, preset, en, reset
  not not_1 (stallIF, or_4_out);
  not not_2 (stallID, or_4_out);
  and and_10 (flushID, in_1, d_ff_1_q);
  D_Flip_Flop #(.trigger("falling")) d_ff_2 (
    .clk(in_1), .D(branch___jump), .Q(d_ff_2_q));  // open: Qn, preset, en, reset
  and and_11 (flushIF, ~in_1, d_ff_2_q);  // AND_Gate

  // Other names for the same wires on the sheet: clock = in_1
endmodule

module regread (
  input  o1,
  input  o2,
  input  o3,
  input  o4,
  input  f1,
  input  f2,
  input  f3,
  output r1read,
  output r2read
);

  wire and_1_out, and_2_out, and_3_out, and_4_out, and_5_out, and_6_out, and_7_out, and_8_out, and_9_out,
       and_10_out, and_11_out, and_12_out, and_13_out, and_14_out, not_1_out, not_2_out, not_3_out,
       not_4_out, not_5_out, not_6_out, not_7_out, not_8_out, not_9_out, not_10_out, not_11_out, not_12_out,
       not_13_out, not_14_out, not_15_out, not_16_out, not_17_out, not_18_out, not_19_out, not_20_out,
       not_21_out, not_22_out;

  not not_1 (not_1_out, o1);
  not not_2 (not_2_out, o2);
  not not_3 (not_3_out, o1);
  not not_4 (not_4_out, o3);
  not not_5 (not_5_out, o1);
  not not_6 (not_6_out, o4);
  not not_7 (not_7_out, o2);
  not not_8 (not_8_out, o3);
  not not_9 (not_9_out, o3);
  not not_10 (not_10_out, o4);
  not not_11 (not_11_out, o3);
  not not_12 (not_12_out, f1);
  not not_13 (not_13_out, o3);
  not not_14 (not_14_out, f2);
  not not_15 (not_15_out, o3);
  not not_16 (not_16_out, f3);
  not not_17 (not_17_out, o1);
  not not_18 (not_18_out, o2);
  not not_19 (not_19_out, o1);
  not not_20 (not_20_out, o4);
  not not_21 (not_21_out, o3);
  not not_22 (not_22_out, o3);
  and and_1 (and_1_out, not_1_out, not_2_out);
  and and_2 (and_2_out, not_3_out, not_4_out);
  and and_3 (and_3_out, not_5_out, not_6_out);
  and and_4 (and_4_out, not_7_out, not_8_out);
  and and_5 (and_5_out, not_9_out, not_10_out);
  and and_6 (and_6_out, o1, o2, o3, o4);
  and and_7 (and_7_out, not_11_out, not_12_out);
  and and_8 (and_8_out, not_13_out, not_14_out);
  and and_9 (and_9_out, not_15_out, not_16_out);
  and and_10 (and_10_out, not_17_out, not_18_out, o4);
  and and_11 (and_11_out, not_19_out, o3, not_20_out);
  and and_12 (and_12_out, o2, not_21_out);
  and and_13 (and_13_out, o1, not_22_out);
  and and_14 (and_14_out, o1, o2, o4);
  or or_1 (r1read, and_1_out, and_2_out, and_3_out, and_4_out, and_5_out, and_6_out);
  or or_2 (r2read, and_7_out, and_8_out, and_9_out, and_10_out, and_11_out, and_12_out, and_13_out, and_14_out);
endmodule
